// Logisim project SoDo-23120262.circ as structural Verilog: 1 circuit, main circuit main
module main (
  input  I0,
  input  I1,
  input  I2,
  input  I3
);

  wire D0_out, D1_out, D2_out, D3_out, D4_out, D5_out, D6_out, I1_nI0_out, I1I0_out, I2_nI0_out, I2_nI1_out,
       I2_nI1I0_out, I2I0_out, nI1_nI0_out, nI2_nI0_out, nI2I1_out, not_1_out, not_2_out, not_3_out;

  not not_1 (not_1_out, I0);
  not not_2 (not_2_out, I1);
  not not_3 (not_3_out, I2);
  and I1_nI0 (I1_nI0_out, not_1_out, I1);
  and nI1_nI0 (nI1_nI0_out, not_1_out, not_2_out);
  and nI2_nI0 (nI2_nI0_out, not_1_out, not_3_out);
  and nI2I1 (nI2I1_out, I1, not_3_out);
  and I2_nI1I0 (I2_nI1I0_out, I0, not_2_out, I2);
  and I2_nI1 (I2_nI1_out, I2, not_2_out);
  and I1I0 (I1I0_out, I0, I1);
  and I2_nI0 (I2_nI0_out, not_1_out, I2);
  and I2I0 (I2I0_out, I2, I0);
  or D0 (D0_out, I3, I2_nI1I0_out, I1_nI0_out, nI2I1_out, nI2_nI0_out);
  or D1 (D1_out, I0, I2, not_2_out);
  or D2 (D2_out, nI2_nI0_out, I1_nI0_out);
  or D3 (D3_out, nI2I1_out, I1_nI0_out, I2_nI1_out, I3);
  or D4 (D4_out, I1I0_out, nI1_nI0_out, not_3_out);
  or D5 (D5_out, I3, I2_nI0_out, I2_nI1_out, nI1_nI0_out);
  or D6 (D6_out, I2I0_out, I3, I1, nI2_nI0_out);
  _7_Segment_Display u_7_segment_display_1 (
    .g(D3_out), .f(D5_out), .a(D6_out), .b(D4_out), .e(D2_out), .d(D0_out), .c(D1_out));  // open: dp

  // Notes on the sheet:
  //   1
endmodule
